// Logisim project Fault-2.circ as structural Verilog: 1 circuit, main circuit main
module main (
  input  in_1,
  input  in_2,
  input  in_3,
  input  in_4,
  output out_5,
  output out_6,
  output out_7,
  output out_8
);

  wire and_1_out, not_1_out, not_2_out, not_3_out, or_1_out, or_2_out, xor_1_out;

  and and_1 (and_1_out, in_1, in_2);
  or or_1 (or_1_out, in_3, in_4);
  not not_1 (not_1_out, and_1_out);
  not not_2 (not_2_out, in_4);
  xor xor_1 (xor_1_out, not_1_out, or_1_out);
  not not_3 (not_3_out, or_1_out);
  or or_2 (or_2_out, or_1_out, or_1_out);
  nor nor_1 (out_6, and_1_out, xor_1_out);
  nand nand_1 (out_8, not_3_out, not_2_out);
  xor xor_2 (out_5, or_2_out, out_6);
  xnor xnor_1 (out_7, out_6, not_3_out);

  // Notes on the sheet:
  //   Circuit 2
endmodule
